# Fritzing sketch lcd_interface (saved by Fritzing 0.6.2b)
stripboards: 1

parts:
  J2 = female pin header, 3 pins [form="♀ (female)"]
  J1 = female pin header, 4 pins [form="♀ (female)"]
  U2 = Voltage Regulator - Variable [package="TO220 [THT]"]

nets:
  N1: J2.pin1, U2.IN
  N2: J2.pin2, J1.pin1, J1.pin2, U2.ADJ, U2.OUT
  N3: J2.pin3, J1.pin4
